// Logisim project RISC-V CYCLE.circ as structural Verilog: 14 circuits, main circuit main
module main (
);

  wire branch_alu_1_output, clock_1_out, controller_1_out_3, controller_1_out_4, controller_1_out_5,
       controller_1_out_6, controller_1_out_7, controller_1_out_12, reset_out;
  wire [1:0] controller_1_out_8, controller_1_out_9, controller_1_out_10;
  wire [2:0] controller_1_out_11;
  wire [3:0] alu_control_1_output;
  wire [9:0] alu_1_output_2;
  wire [31:0] adder_1_out, alu_1_output, immidiate_gentration_1_i_type, immidiate_gentration_1_s_type,
       immidiate_gentration_1_sb_type, immidiate_gentration_1_u_type, immidiate_gentration_1_uj_type,
       multiplexer_1_out, multiplexer_2_out, multiplexer_3_out, multiplexer_4_out, multiplexer_5_out,
       multiplexer_6_out, PC_q, ram_1_data, register_file_1_rs_1, register_file_1_rs_2, rom_1_data;

  Clock clock_1 (.out(clock_1_out));
  Button reset (.out(reset_out));
  Multiplexer #(.select(2), .width(32)) multiplexer_1 (
    .in0(adder_1_out), .in1(immidiate_gentration_1_sb_type), .in2(immidiate_gentration_1_uj_type),
    .in3({alu_1_output[31:12], alu_1_output_2, alu_1_output[1:0]}), .out(multiplexer_1_out),
    .sel(controller_1_out_9));  // open: en
  Register #(.width(32)) PC (.D(multiplexer_1_out), .Q(PC_q), .clk(clock_1_out), .clr(reset_out));  // open: en
  Adder #(.width(32)) adder_1 (.a(32'h4), .b(PC_q), .out(adder_1_out));  // open: cin, cout
  ROM #(.addrWidth(10), .dataWidth(32)) rom_1 (.addr(PC_q[11:2]), .data(rom_1_data));  // open: sel
  Immidiate_gentration immidiate_gentration_1 (
    .instruction(rom_1_data), .PC(PC_q), .I_TYPE(immidiate_gentration_1_i_type),
    .S_TYPE(immidiate_gentration_1_s_type), .SB_TYPE(immidiate_gentration_1_sb_type),
    .U_TYPE(immidiate_gentration_1_u_type), .UJ_TYPE(immidiate_gentration_1_uj_type));
  Multiplexer #(.select(2), .width(32)) multiplexer_2 (
    .in0(immidiate_gentration_1_i_type), .in1(immidiate_gentration_1_s_type),
    .in2(immidiate_gentration_1_u_type), .out(multiplexer_2_out), .sel(controller_1_out_10));  // open: in3, en
  controller controller_1 (
    .in_1(rom_1_data[6:0]), .out_4(controller_1_out_4), .in_2(branch_alu_1_output),
    .out_3(controller_1_out_3), .out_5(controller_1_out_5), .out_7(controller_1_out_7),
    .out_6(controller_1_out_6), .out_8(controller_1_out_8), .out_9(controller_1_out_9),
    .out_10(controller_1_out_10), .out_11(controller_1_out_11), .out_12(controller_1_out_12));
  Register_File register_file_1 (
    .rd(multiplexer_6_out), .in_2(reset_out), .en(controller_1_out_7), .rs_1(register_file_1_rs_1),
    .rs_2(register_file_1_rs_2), .rd_sel(rom_1_data[11:7]), .in_3(clock_1_out), .rs_1_sel(rom_1_data[19:15]),
    .rs_2_sel(rom_1_data[24:20]));
  Multiplexer #(.select(2), .width(32)) multiplexer_3 (
    .in0(register_file_1_rs_1), .in1(adder_1_out), .in2(PC_q), .out(multiplexer_3_out),
    .sel(controller_1_out_8));  // open: in3, en
  Multiplexer #(.width(32)) multiplexer_4 (
    .in0(register_file_1_rs_2), .in1(multiplexer_2_out), .out(multiplexer_4_out), .sel(controller_1_out_3));  // open: en
  ALU_Control alu_control_1 (
    .ALU_OP(controller_1_out_11), .FUNCT3(rom_1_data[14:12]), .FUNCT7(rom_1_data[30]),
    .OUTPUT(alu_control_1_output));
  Branch_ALU branch_alu_1 (
    .A(register_file_1_rs_1), .B(register_file_1_rs_2), .\output (branch_alu_1_output),
    .funct3(rom_1_data[14:12]));
  ALU alu_1 (
    .OUTPUT({alu_1_output[31:12], alu_1_output_2, alu_1_output[1:0]}), .Operand_A(multiplexer_3_out),
    .Operand_B(multiplexer_4_out), .ALU_control(alu_control_1_output));  // open: Carry
  RAM #(.addrWidth(10), .dataWidth(32), .bus("separate")) ram_1 (
    .addr(alu_1_output_2), .din(register_file_1_rs_2), .data(ram_1_data), .str(controller_1_out_4),
    .clk(clock_1_out), .ld(controller_1_out_5));  // open: sel, clr
  Multiplexer #(.width(32)) multiplexer_5 (
    .in0(ram_1_data), .in1({alu_1_output[31:12], alu_1_output_2, alu_1_output[1:0]}),
    .out(multiplexer_5_out), .sel(controller_1_out_6));  // open: en
  Multiplexer #(.width(32)) multiplexer_6 (
    .in0(multiplexer_5_out), .in1(adder_1_out), .out(multiplexer_6_out), .sel(controller_1_out_12));  // open: en

  // Notes on the sheet:
  //   PROGRAM MEMORY
  //   contents of rom_1 (hex, n*v repeats v):
  //   52083 452103 1b3 a203 4181b3 408093 fff10113 fe0118e3 352423
endmodule

module Program_Counter (
);

  wire clock_1_out, reset_out;
  wire [31:0] adder_1_out, PC_q;

  Register #(.width(32)) PC (.D(adder_1_out), .Q(PC_q), .clk(clock_1_out), .clr(reset_out));  // open: en
  Clock clock_1 (.out(clock_1_out));
  Button reset (.out(reset_out));
  Adder #(.width(32)) adder_1 (.a(32'h4), .b(PC_q), .out(adder_1_out));  // open: cin, cout
  ROM #(.addrWidth(10), .dataWidth(32)) rom_1 (.addr(PC_q[11:2]));  // open: data, sel

  // Notes on the sheet:
  //   PROGRAM MEMORY
  //   contents of rom_1 (hex, n*v repeats v):
  //   500513 600593 b50633
endmodule

module ALU (
  input  [31:0] Operand_A,
  input  [31:0] Operand_B,
  input  [3:0] ALU_control,
  output Carry,
  output [31:0] OUTPUT
);

  wire comparator_1_lt;
  wire [31:0] _0010_out, _0011_out, _0110_out, adder_1_out, multiplexer_1_out, shifter_1_out, shifter_2_out,
       shifter_3_out, subtractor_1_out;

  Adder #(.width(32)) adder_1 (.a(Operand_A), .b(Operand_B), .out(adder_1_out), .cout(Carry));  // open: cin
  Subtractor #(.width(32)) subtractor_1 (.a(Operand_A), .b(Operand_B), .out(subtractor_1_out));  // open: bin, bout
  assign _0010_out = Operand_A & Operand_B;  // AND_Gate _0010, 32 bits wide
  assign _0011_out = Operand_A | Operand_B;  // OR_Gate _0011, 32 bits wide
  assign _0110_out = Operand_A ^ Operand_B;  // XOR_Gate _0110, 32 bits wide
  Shifter #(.width(32)) shifter_1 (.in(Operand_A), .\dist (Operand_B[4:0]), .out(shifter_1_out));
  Shifter #(.width(32), .shift("lr")) shifter_2 (.in(Operand_A), .\dist (Operand_B[4:0]), .out(shifter_2_out));
  Shifter #(.width(32), .shift("ar")) shifter_3 (.in(Operand_A), .\dist (Operand_B[4:0]), .out(shifter_3_out));
  Comparator #(.width(32)) comparator_1 (.a(Operand_A), .b(Operand_B), .lt(comparator_1_lt));  // open: gt, eq
  Multiplexer #(.width(32)) multiplexer_1 (
    .in1(32'h1), .out(multiplexer_1_out), .sel(comparator_1_lt));  // open: in0, en
  Multiplexer #(.select(4), .width(32)) multiplexer_2 (
    .in0(adder_1_out), .in1(subtractor_1_out), .in2(_0010_out), .in3(_0011_out), .in4(_0110_out),
    .in5(shifter_1_out), .in6(shifter_2_out), .in7(shifter_3_out), .in8(multiplexer_1_out), .out(OUTPUT),
    .sel(ALU_control));  // open: in9, in10, in11, in12, in13, in14, in15, en
endmodule

module Register_File (
  input  [31:0] rd,
  input  in_2,
  input  in_3,
  input  en,
  input  [4:0] rd_sel,
  input  [4:0] rs_1_sel,
  input  [4:0] rs_2_sel,
  output [31:0] rs_1,
  output [31:0] rs_2
);

  wire decoder_1_out0, decoder_1_out1, decoder_1_out2, decoder_1_out3, decoder_1_out4, decoder_1_out5,
       decoder_1_out6, decoder_1_out7, decoder_1_out8, decoder_1_out9, decoder_1_out10, decoder_1_out11,
       decoder_1_out12, decoder_1_out13, decoder_1_out14, decoder_1_out15, decoder_1_out16, decoder_1_out17,
       decoder_1_out18, decoder_1_out19, decoder_1_out20, decoder_1_out21, decoder_1_out22, decoder_1_out23,
       decoder_1_out24, decoder_1_out25, decoder_1_out26, decoder_1_out27, decoder_1_out28, decoder_1_out29,
       decoder_1_out30, decoder_1_out31;
  wire [31:0] register_1_q, register_2_q, register_3_q, register_4_q, register_5_q, register_6_q,
       register_7_q, register_8_q, register_9_q, register_10_q, register_11_q, register_12_q, register_13_q,
       register_14_q, register_15_q, register_16_q, register_17_q, register_18_q, register_19_q,
       register_20_q, register_21_q, register_22_q, register_23_q, register_24_q, register_25_q,
       register_26_q, register_27_q, register_28_q, register_29_q, register_30_q, register_31_q,
       register_32_q;

  Decoder #(.select(5)) decoder_1 (
    .out0(decoder_1_out0), .out1(decoder_1_out1), .out2(decoder_1_out2), .out3(decoder_1_out3),
    .out4(decoder_1_out4), .out5(decoder_1_out5), .out6(decoder_1_out6), .out7(decoder_1_out7),
    .out8(decoder_1_out8), .out9(decoder_1_out9), .out10(decoder_1_out10), .out11(decoder_1_out11),
    .out12(decoder_1_out12), .out13(decoder_1_out13), .out14(decoder_1_out14), .out15(decoder_1_out15),
    .out16(decoder_1_out16), .out17(decoder_1_out17), .out18(decoder_1_out18), .out19(decoder_1_out19),
    .out20(decoder_1_out20), .out21(decoder_1_out21), .out22(decoder_1_out22), .out23(decoder_1_out23),
    .out24(decoder_1_out24), .out25(decoder_1_out25), .out26(decoder_1_out26), .out27(decoder_1_out27),
    .out28(decoder_1_out28), .out29(decoder_1_out29), .out30(decoder_1_out30), .out31(decoder_1_out31),
    .sel(rd_sel), .en(en));
  Button RESET (.out(in_2));
  Clock clock (.out(in_3));
  Register #(.width(32)) register_1 (.D(rd), .en(decoder_1_out0), .Q(register_1_q), .clk(in_3), .clr(in_2));
  Register #(.width(32)) register_2 (.D(rd), .en(decoder_1_out1), .Q(register_2_q), .clk(in_3), .clr(in_2));
  Register #(.width(32)) register_3 (.D(rd), .en(decoder_1_out2), .Q(register_3_q), .clk(in_3), .clr(in_2));
  Register #(.width(32)) register_4 (.D(rd), .en(decoder_1_out3), .Q(register_4_q), .clk(in_3), .clr(in_2));
  Register #(.width(32)) register_5 (.D(rd), .en(decoder_1_out4), .Q(register_5_q), .clk(in_3), .clr(in_2));
  Register #(.width(32)) register_6 (.D(rd), .en(decoder_1_out5), .Q(register_6_q), .clk(in_3), .clr(in_2));
  Register #(.width(32)) register_7 (.D(rd), .en(decoder_1_out6), .Q(register_7_q), .clk(in_3), .clr(in_2));
  Register #(.width(32)) register_8 (.D(rd), .en(decoder_1_out7), .Q(register_8_q), .clk(in_3), .clr(in_2));
  Register #(.width(32)) register_9 (.D(rd), .en(decoder_1_out8), .Q(register_9_q), .clk(in_3), .clr(in_2));
  Register #(.width(32)) register_10 (.D(rd), .en(decoder_1_out9), .Q(register_10_q), .clk(in_3), .clr(in_2));
  Register #(.width(32)) register_11 (.D(rd), .en(decoder_1_out10), .Q(register_11_q), .clk(in_3), .clr(in_2));
  Register #(.width(32)) register_12 (.D(rd), .en(decoder_1_out11), .Q(register_12_q), .clk(in_3), .clr(in_2));
  Register #(.width(32)) register_13 (.D(rd), .en(decoder_1_out12), .Q(register_13_q), .clk(in_3), .clr(in_2));
  Register #(.width(32)) register_14 (.D(rd), .en(decoder_1_out13), .Q(register_14_q), .clk(in_3), .clr(in_2));
  Register #(.width(32)) register_15 (.D(rd), .en(decoder_1_out14), .Q(register_15_q), .clk(in_3), .clr(in_2));
  Register #(.width(32)) register_16 (.D(rd), .en(decoder_1_out15), .Q(register_16_q), .clk(in_3), .clr(in_2));
  Register #(.width(32)) register_17 (.D(rd), .en(decoder_1_out16), .Q(register_17_q), .clk(in_3), .clr(in_2));
  Register #(.width(32)) register_18 (.D(rd), .en(decoder_1_out17), .Q(register_18_q), .clk(in_3), .clr(in_2));
  Register #(.width(32)) register_19 (.D(rd), .en(decoder_1_out18), .Q(register_19_q), .clk(in_3), .clr(in_2));
  Register #(.width(32)) register_20 (.D(rd), .en(decoder_1_out19), .Q(register_20_q), .clk(in_3), .clr(in_2));
  Register #(.width(32)) register_21 (.D(rd), .en(decoder_1_out20), .Q(register_21_q), .clk(in_3), .clr(in_2));
  Register #(.width(32)) register_22 (.D(rd), .en(decoder_1_out21), .Q(register_22_q), .clk(in_3), .clr(in_2));
  Register #(.width(32)) register_23 (.D(rd), .en(decoder_1_out22), .Q(register_23_q), .clk(in_3), .clr(in_2));
  Register #(.width(32)) register_24 (.D(rd), .en(decoder_1_out23), .Q(register_24_q), .clk(in_3), .clr(in_2));
  Register #(.width(32)) register_25 (.D(rd), .en(decoder_1_out24), .Q(register_25_q), .clk(in_3), .clr(in_2));
  Register #(.width(32)) register_26 (.D(rd), .en(decoder_1_out25), .Q(register_26_q), .clk(in_3), .clr(in_2));
  Register #(.width(32)) register_27 (.D(rd), .en(decoder_1_out26), .Q(register_27_q), .clk(in_3), .clr(in_2));
  Register #(.width(32)) register_28 (.D(rd), .en(decoder_1_out27), .Q(register_28_q), .clk(in_3), .clr(in_2));
  Register #(.width(32)) register_29 (.D(rd), .en(decoder_1_out28), .Q(register_29_q), .clk(in_3), .clr(in_2));
  Register #(.width(32)) register_30 (.D(rd), .en(decoder_1_out29), .Q(register_30_q), .clk(in_3), .clr(in_2));
  Register #(.width(32)) register_31 (.D(rd), .en(decoder_1_out30), .Q(register_31_q), .clk(in_3), .clr(in_2));
  Register #(.width(32)) register_32 (.D(rd), .en(decoder_1_out31), .Q(register_32_q), .clk(in_3), .clr(in_2));
  Multiplexer #(.select(5), .width(32)) multiplexer_1 (
    .in0(register_1_q), .in1(register_2_q), .in2(register_3_q), .in3(register_4_q), .in4(register_5_q),
    .in5(register_6_q), .in6(register_7_q), .in7(register_8_q), .in8(register_9_q), .in9(register_10_q),
    .in10(register_11_q), .in11(register_12_q), .in12(register_13_q), .in13(register_14_q),
    .in14(register_15_q), .in15(register_16_q), .in16(register_17_q), .in17(register_18_q),
    .in18(register_19_q), .in19(register_20_q), .in20(register_21_q), .in21(register_22_q),
    .in22(register_23_q), .in23(register_24_q), .in24(register_25_q), .in25(register_26_q),
    .in26(register_27_q), .in27(register_28_q), .in28(register_29_q), .in29(register_30_q),
    .in30(register_31_q), .in31(register_32_q), .out(rs_1), .sel(rs_1_sel));  // open: en
  Multiplexer #(.select(5), .width(32)) multiplexer_2 (
    .in0(register_1_q), .in1(register_2_q), .in2(register_3_q), .in3(register_4_q), .in4(register_5_q),
    .in5(register_6_q), .in6(register_7_q), .in7(register_8_q), .in8(register_9_q), .in9(register_10_q),
    .in10(register_11_q), .in11(register_12_q), .in12(register_13_q), .in13(register_14_q),
    .in14(register_15_q), .in15(register_16_q), .in16(register_17_q), .in17(register_18_q),
    .in18(register_19_q), .in19(register_20_q), .in20(register_21_q), .in21(register_22_q),
    .in22(register_23_q), .in23(register_24_q), .in24(register_25_q), .in25(register_26_q),
    .in26(register_27_q), .in27(register_28_q), .in28(register_29_q), .in29(register_30_q),
    .in30(register_31_q), .in31(register_32_q), .out(rs_2), .sel(rs_2_sel));  // open: en
endmodule

module Branch_ALU (
  input  [31:0] A,
  input  [31:0] B,
  input  [2:0] funct3,
  output \output 
);

  wire comparator_1_eq, comparator_1_gt, comparator_1_lt, comparator_2_eq, comparator_2_gt, comparator_2_lt,
       not_1_out, or_1_out, or_2_out;

  Comparator #(.width(32), .mode("unsigned")) comparator_1 (
    .a(A), .b(B), .gt(comparator_1_gt), .eq(comparator_1_eq), .lt(comparator_1_lt));
  Comparator #(.width(32)) comparator_2 (
    .a(A), .b(B), .gt(comparator_2_gt), .eq(comparator_2_eq), .lt(comparator_2_lt));
  or or_1 (or_1_out, comparator_1_gt, comparator_1_eq);
  or or_2 (or_2_out, comparator_2_gt, comparator_2_eq);
  not not_1 (not_1_out, comparator_2_eq);
  Multiplexer #(.select(3)) multiplexer_1 (
    .in0(or_2_out), .in1(not_1_out), .in2(comparator_2_eq), .in3(comparator_2_lt), .in4(or_1_out),
    .in5(comparator_1_lt), .out(\output ), .sel(funct3));  // open: in6, in7, en
endmodule

module ALU_Control (
  input  [2:0] ALU_OP,
  input  [2:0] FUNCT3,
  input  FUNCT7,
  output [3:0] OUTPUT
);

  wire and_1_out, and_2_out, and_3_out, and_4_out, and_5_out, and_6_out, and_7_out, and_8_out, and_9_out,
       and_10_out, and_11_out, and_12_out, and_13_out, and_14_out, not_1_out, not_2_out, not_3_out,
       not_4_out, not_5_out, not_6_out, not_7_out, not_8_out, not_9_out, not_10_out, not_11_out, not_12_out;

  not not_1 (not_1_out, ALU_OP[0]);
  not not_2 (not_2_out, ALU_OP[2]);
  not not_3 (not_3_out, FUNCT3[0]);
  not not_4 (not_4_out, FUNCT3[1]);
  not not_5 (not_5_out, FUNCT3[1]);
  not not_6 (not_6_out, FUNCT3[0]);
  not not_7 (not_7_out, FUNCT3[1]);
  not not_8 (not_8_out, FUNCT3[0]);
  not not_9 (not_9_out, FUNCT3[0]);
  not not_10 (not_10_out, FUNCT3[1]);
  not not_11 (not_11_out, FUNCT7);
  not not_12 (not_12_out, FUNCT3[2]);
  and and_1 (and_1_out, not_1_out, not_2_out, not_3_out, FUNCT3[1]);
  and and_2 (and_2_out, ALU_OP[0], ALU_OP[1]);
  and and_3 (and_3_out, not_4_out, FUNCT3[2]);
  and and_4 (and_4_out, FUNCT3[0], not_5_out);
  and and_5 (and_5_out, ALU_OP[0], ALU_OP[1]);
  and and_6 (and_6_out, not_6_out, not_7_out, FUNCT3[2]);
  and and_7 (and_7_out, FUNCT3[0], FUNCT7);
  and and_8 (and_8_out, FUNCT3[0], FUNCT3[1]);
  and and_9 (and_9_out, ALU_OP[0], ALU_OP[1]);
  and and_10 (and_10_out, not_8_out, FUNCT7);
  and and_11 (and_11_out, not_9_out, FUNCT3[2]);
  and and_12 (and_12_out, not_10_out, FUNCT3[2], not_11_out);
  and and_13 (and_13_out, FUNCT3[0], FUNCT3[1], not_12_out);
  and and_14 (and_14_out, ALU_OP[0], ALU_OP[1], ALU_OP[2]);
  or or_1 (OUTPUT[3], and_1_out, and_2_out);
  or or_2 (OUTPUT[2], and_3_out, and_4_out, and_5_out);
  or or_3 (OUTPUT[1], and_6_out, and_7_out, and_8_out, and_9_out);
  or or_4 (OUTPUT[0], and_10_out, and_11_out, and_12_out, and_13_out, and_14_out);
endmodule

module Immidiate_gentration (
  input  [31:0] instruction,
  input  [31:0] PC,
  output [31:0] I_TYPE,
  output [31:0] S_TYPE,
  output [31:0] SB_TYPE,
  output [31:0] U_TYPE,
  output [31:0] UJ_TYPE
);

  assign I_TYPE[31:12] = {{19{1'b0}}, instruction[31]};  // Bit_Extender bit_extender_1
  Adder #(.width(32)) adder_1 (
    .a({I_TYPE[31:12], instruction[31:25], instruction[7], instruction[11:8]}), .b(PC), .out(SB_TYPE));  // open: cin, cout
  Adder #(.width(32)) adder_2 (
    .a(PC), .b({I_TYPE[23:12], instruction[31], instruction[19:12], instruction[20], instruction[30:21]}),
    .out(UJ_TYPE));  // open: cin, cout

  assign I_TYPE[11:0] = instruction[31:20];
  assign S_TYPE = {I_TYPE[31:12], instruction[31:25], instruction[11:7]};
  assign U_TYPE = {I_TYPE[23:12], instruction[31:12]};
endmodule

module controller (
  input  [6:0] in_1,
  input  in_2,
  output out_3,
  output out_4,
  output out_5,
  output out_6,
  output out_7,
  output [1:0] out_8,
  output [1:0] out_9,
  output [1:0] out_10,
  output [2:0] out_11,
  output out_12
);

  wire type_decode_1_auipc, type_decode_1_b_type, type_decode_1_i_type, type_decode_1_jal,
       type_decode_1_jalr, type_decode_1_lui, type_decode_1_lw, type_decode_1_r_type, type_decode_1_s_type;

  type_decode type_decode_1 (
    .Opcode(in_1), .R_TYPE(type_decode_1_r_type), .I_TYPE(type_decode_1_i_type),
    .S_TYPE(type_decode_1_s_type), .B_TYPE(type_decode_1_b_type), .LUI(type_decode_1_lui),
    .AUIPC(type_decode_1_auipc), .JAL(type_decode_1_jal), .JALR(type_decode_1_jalr), .LW(type_decode_1_lw));
  control_decode control_decode_1 (
    .B_TYPE(type_decode_1_b_type), .BOUT(in_2), .OP_B_SEL(out_3), .MEM_WRITE(out_4), .MEM__READ(out_5),
    .WRITE_BACK(out_6), .REG_FILE_EN(out_7), .OP_A_SEL(out_8), .PC_SEL(out_9), .IMM_SEL(out_10),
    .ALU_OP(out_11), .JALR_2(out_12), .R_TYPE(type_decode_1_r_type), .I_TYPE(type_decode_1_i_type),
    .S_TYPE(type_decode_1_s_type), .LUI(type_decode_1_lui), .AUIPC(type_decode_1_auipc),
    .JAL(type_decode_1_jal), .JALR(type_decode_1_jalr), .LW(type_decode_1_lw));
endmodule

module type_decode (
  input  [6:0] Opcode,
  output R_TYPE,
  output I_TYPE,
  output S_TYPE,
  output B_TYPE,
  output LUI,
  output AUIPC,
  output JAL,
  output JALR,
  output LW
);

  Comparator #(.width(7)) comparator_1 (.a(7'b0110011), .b(Opcode), .eq(R_TYPE));  // open: gt, lt
  Comparator #(.width(7)) comparator_2 (.a(7'b0010011), .b(Opcode), .eq(I_TYPE));  // open: gt, lt
  Comparator #(.width(7)) comparator_3 (.a(7'b0100011), .b(Opcode), .eq(S_TYPE));  // open: gt, lt
  Comparator #(.width(7)) comparator_4 (.a(7'b1100011), .b(Opcode), .eq(B_TYPE));  // open: gt, lt
  Comparator #(.width(7)) comparator_5 (.a(7'b0110111), .b(Opcode), .eq(LUI));  // open: gt, lt
  Comparator #(.width(7)) comparator_6 (.a(7'b0010111), .b(Opcode), .eq(AUIPC));  // open: gt, lt
  Comparator #(.width(7)) comparator_7 (.a(7'b1101111), .b(Opcode), .eq(JAL));  // open: gt, lt
  Comparator #(.width(7)) comparator_8 (.a(7'b1100111), .b(Opcode), .eq(JALR));  // open: gt, lt
  Comparator #(.width(7)) comparator_9 (.a(7'b0000011), .b(Opcode), .eq(LW));  // open: gt, lt
endmodule

module control_decode (
  input  B_TYPE,
  input  R_TYPE,
  input  I_TYPE,
  input  S_TYPE,
  input  LUI,
  input  AUIPC,
  input  JAL,
  input  JALR,
  input  LW,
  input  BOUT,
  output OP_B_SEL,
  output MEM_WRITE,
  output MEM__READ,
  output WRITE_BACK,
  output REG_FILE_EN,
  output [1:0] OP_A_SEL,
  output [1:0] PC_SEL,
  output [1:0] IMM_SEL,
  output [2:0] ALU_OP,
  output JALR_2
);

  wire and_1_out;

  and and_1 (and_1_out, B_TYPE, BOUT);
  or or_1 (OP_B_SEL, I_TYPE, S_TYPE, LUI, AUIPC, JALR, LW);
  or or_2 (REG_FILE_EN, R_TYPE, I_TYPE, LUI, AUIPC, JAL, JALR, LW);
  OP_A_SEL op_a_sel_1 (.OP_A_SEL(OP_A_SEL), .LUI(LUI), .AUIPC(AUIPC), .JAL(JAL));
  PC_SEL pc_sel_1 (.out_4(PC_SEL), .B(and_1_out), .JAL(JAL), .JALR(JALR));
  IMM_SEL imm_sel_1 (.R(R_TYPE), .S(S_TYPE), .B(and_1_out), .LUI(LUI), .AUIPC(AUIPC), .JAL(JAL), .out_7(IMM_SEL));
  ALU_OP alu_op_1 (.I(I_TYPE), .S(S_TYPE), .AUIPC(AUIPC), .LUI(LUI), .LW(LW), .JALR(JALR), .JAL(JAL), .ALU_OP(ALU_OP));

  assign JALR_2 = JALR;
  assign MEM__READ = LW;
  assign MEM_WRITE = S_TYPE;
  assign WRITE_BACK = LW;
endmodule

module OP_A_SEL (
  input  LUI,
  input  AUIPC,
  input  JAL,
  output [1:0] OP_A_SEL
);

  wire and_1_out, and_2_out, and_3_out, and_4_out, not_1_out, not_2_out, not_3_out;

  not not_1 (not_1_out, LUI);
  not not_2 (not_2_out, AUIPC);
  not not_3 (not_3_out, JAL);
  and and_1 (and_1_out, not_1_out, not_2_out, JAL);
  and and_2 (and_2_out, LUI, not_2_out, not_3_out);
  and and_3 (and_3_out, not_1_out, AUIPC, not_3_out);
  and and_4 (and_4_out, LUI, not_2_out, not_3_out);
  or or_1 (OP_A_SEL[1], and_1_out, and_2_out);
  or or_2 (OP_A_SEL[0], and_3_out, and_4_out);
endmodule

module PC_SEL (
  input  B,
  input  JAL,
  input  JALR,
  output [1:0] out_4
);

  wire and_1_out, and_2_out, and_3_out, not_1_out, not_2_out, not_3_out;

  not not_1 (not_1_out, B);
  not not_2 (not_2_out, JAL);
  not not_3 (not_3_out, JALR);
  and and_1 (and_1_out, not_1_out, not_2_out, JALR);
  and and_2 (and_2_out, not_1_out, JAL, not_3_out);
  and and_3 (and_3_out, B, not_2_out, not_3_out);
  or or_1 (out_4[1], and_1_out, and_2_out);
  or or_2 (out_4[0], and_1_out, and_3_out);
endmodule

module IMM_SEL (
  input  R,
  input  S,
  input  B,
  input  LUI,
  input  AUIPC,
  input  JAL,
  output [1:0] out_7
);

  wire and_1_out, and_2_out, and_3_out, and_4_out, and_5_out, and_6_out, and_7_out, and_8_out, and_9_out,
       not_1_out, not_2_out, not_3_out, not_4_out, not_5_out, not_6_out, not_7_out, not_8_out, not_9_out,
       not_10_out, not_11_out, not_12_out, not_13_out, not_14_out, not_15_out, not_16_out, not_17_out,
       not_18_out, not_19_out, not_20_out, not_21_out, not_22_out, not_23_out, not_24_out, not_25_out,
       not_26_out, not_27_out, not_28_out, not_29_out, not_30_out, not_31_out, not_32_out, not_33_out,
       not_34_out, not_35_out, not_36_out, not_37_out, not_38_out, not_39_out, not_40_out, not_41_out,
       not_42_out, not_43_out, not_44_out, not_45_out;

  not not_1 (not_1_out, R);
  not not_2 (not_2_out, S);
  not not_3 (not_3_out, B);
  not not_4 (not_4_out, LUI);
  not not_5 (not_5_out, AUIPC);
  not not_6 (not_6_out, R);
  not not_7 (not_7_out, S);
  not not_8 (not_8_out, B);
  not not_9 (not_9_out, LUI);
  not not_10 (not_10_out, JAL);
  not not_11 (not_11_out, R);
  not not_12 (not_12_out, S);
  not not_13 (not_13_out, B);
  not not_14 (not_14_out, AUIPC);
  not not_15 (not_15_out, JAL);
  not not_16 (not_16_out, R);
  not not_17 (not_17_out, S);
  not not_18 (not_18_out, LUI);
  not not_19 (not_19_out, AUIPC);
  not not_20 (not_20_out, JAL);
  not not_21 (not_21_out, S);
  not not_22 (not_22_out, B);
  not not_23 (not_23_out, LUI);
  not not_24 (not_24_out, AUIPC);
  not not_25 (not_25_out, JAL);
  not not_26 (not_26_out, R);
  not not_27 (not_27_out, S);
  not not_28 (not_28_out, B);
  not not_29 (not_29_out, LUI);
  not not_30 (not_30_out, AUIPC);
  not not_31 (not_31_out, R);
  not not_32 (not_32_out, S);
  not not_33 (not_33_out, LUI);
  not not_34 (not_34_out, AUIPC);
  not not_35 (not_35_out, JAL);
  not not_36 (not_36_out, R);
  not not_37 (not_37_out, B);
  not not_38 (not_38_out, LUI);
  not not_39 (not_39_out, AUIPC);
  not not_40 (not_40_out, JAL);
  not not_41 (not_41_out, S);
  not not_42 (not_42_out, B);
  not not_43 (not_43_out, LUI);
  not not_44 (not_44_out, AUIPC);
  not not_45 (not_45_out, JAL);
  and and_1 (and_1_out, not_1_out, not_2_out, not_3_out, not_4_out, not_5_out, JAL);
  and and_2 (and_2_out, not_6_out, not_7_out, not_8_out, not_9_out, AUIPC, not_10_out);
  and and_3 (and_3_out, not_11_out, not_12_out, not_13_out, LUI, not_14_out, not_15_out);
  and and_4 (and_4_out, not_16_out, not_17_out, B, not_18_out, not_19_out, not_20_out);
  and and_5 (and_5_out, R, not_21_out, not_22_out, not_23_out, not_24_out, not_25_out);
  and and_6 (and_6_out, not_26_out, not_27_out, not_28_out, not_29_out, not_30_out, JAL);
  and and_7 (and_7_out, not_31_out, not_32_out, B, not_33_out, not_34_out, not_35_out);
  and and_8 (and_8_out, not_36_out, S, not_37_out, not_38_out, not_39_out, not_40_out);
  and and_9 (and_9_out, R, not_41_out, not_42_out, not_43_out, not_44_out, not_45_out);
  or or_1 (out_7[1], and_1_out, and_2_out, and_3_out, and_4_out, and_5_out);
  or or_2 (out_7[0], and_6_out, and_7_out, and_8_out, and_9_out);
endmodule

module ALU_OP (
  input  I,
  input  S,
  input  AUIPC,
  input  LUI,
  input  LW,
  input  JALR,
  input  JAL,
  output [2:0] ALU_OP
);

  wire and_1_out, and_2_out, and_3_out, and_4_out, and_5_out, and_6_out, and_7_out, and_8_out, and_9_out,
       and_10_out, and_11_out, and_12_out, not_1_out, not_2_out, not_3_out, not_4_out, not_5_out, not_6_out,
       not_7_out, not_8_out, not_9_out, not_10_out, not_11_out, not_12_out, not_13_out, not_14_out,
       not_15_out, not_16_out, not_17_out, not_18_out, not_19_out, not_20_out, not_21_out, not_22_out,
       not_23_out, not_24_out, not_25_out, not_26_out, not_27_out, not_28_out, not_29_out, not_30_out,
       not_31_out, not_32_out, not_33_out, not_34_out, not_35_out, not_36_out, not_37_out, not_38_out,
       not_39_out, not_40_out, not_41_out, not_42_out, not_43_out, not_44_out, not_45_out, not_46_out,
       not_47_out, not_48_out, not_49_out, not_50_out, not_51_out, not_52_out, not_53_out, not_54_out,
       not_55_out, not_56_out, not_57_out, not_58_out, not_59_out, not_60_out, not_61_out, not_62_out,
       not_63_out, not_64_out, not_65_out, not_66_out, not_67_out, not_68_out, not_69_out, not_70_out,
       not_71_out, not_72_out;

  not not_1 (not_1_out, I);
  not not_2 (not_2_out, S);
  not not_3 (not_3_out, AUIPC);
  not not_4 (not_4_out, LUI);
  not not_5 (not_5_out, LW);
  not not_6 (not_6_out, JALR);
  not not_7 (not_7_out, I);
  not not_8 (not_8_out, S);
  not not_9 (not_9_out, AUIPC);
  not not_10 (not_10_out, LW);
  not not_11 (not_11_out, JALR);
  not not_12 (not_12_out, JAL);
  not not_13 (not_13_out, I);
  not not_14 (not_14_out, S);
  not not_15 (not_15_out, LUI);
  not not_16 (not_16_out, LW);
  not not_17 (not_17_out, JALR);
  not not_18 (not_18_out, JAL);
  not not_19 (not_19_out, I);
  not not_20 (not_20_out, AUIPC);
  not not_21 (not_21_out, LUI);
  not not_22 (not_22_out, LW);
  not not_23 (not_23_out, JALR);
  not not_24 (not_24_out, JAL);
  not not_25 (not_25_out, I);
  not not_26 (not_26_out, S);
  not not_27 (not_27_out, AUIPC);
  not not_28 (not_28_out, LUI);
  not not_29 (not_29_out, LW);
  not not_30 (not_30_out, JALR);
  not not_31 (not_31_out, I);
  not not_32 (not_32_out, S);
  not not_33 (not_33_out, AUIPC);
  not not_34 (not_34_out, LUI);
  not not_35 (not_35_out, LW);
  not not_36 (not_36_out, JAL);
  not not_37 (not_37_out, I);
  not not_38 (not_38_out, S);
  not not_39 (not_39_out, AUIPC);
  not not_40 (not_40_out, LW);
  not not_41 (not_41_out, JALR);
  not not_42 (not_42_out, JAL);
  not not_43 (not_43_out, S);
  not not_44 (not_44_out, AUIPC);
  not not_45 (not_45_out, LUI);
  not not_46 (not_46_out, LW);
  not not_47 (not_47_out, JALR);
  not not_48 (not_48_out, JAL);
  not not_49 (not_49_out, I);
  not not_50 (not_50_out, S);
  not not_51 (not_51_out, AUIPC);
  not not_52 (not_52_out, LUI);
  not not_53 (not_53_out, LW);
  not not_54 (not_54_out, JALR);
  not not_55 (not_55_out, I);
  not not_56 (not_56_out, S);
  not not_57 (not_57_out, AUIPC);
  not not_58 (not_58_out, LUI);
  not not_59 (not_59_out, LW);
  not not_60 (not_60_out, JAL);
  not not_61 (not_61_out, I);
  not not_62 (not_62_out, S);
  not not_63 (not_63_out, AUIPC);
  not not_64 (not_64_out, LUI);
  not not_65 (not_65_out, JALR);
  not not_66 (not_66_out, JAL);
  not not_67 (not_67_out, I);
  not not_68 (not_68_out, S);
  not not_69 (not_69_out, LUI);
  not not_70 (not_70_out, LW);
  not not_71 (not_71_out, JALR);
  not not_72 (not_72_out, JAL);
  and and_1 (and_1_out, not_1_out, not_2_out, not_3_out, not_4_out, not_5_out, not_6_out, JAL);
  and and_2 (and_2_out, not_7_out, not_8_out, not_9_out, LUI, not_10_out, not_11_out, not_12_out);
  and and_3 (and_3_out, not_13_out, not_14_out, AUIPC, not_15_out, not_16_out, not_17_out, not_18_out);
  and and_4 (and_4_out, not_19_out, S, not_20_out, not_21_out, not_22_out, not_23_out, not_24_out);
  and and_5 (and_5_out, not_25_out, not_26_out, not_27_out, not_28_out, not_29_out, not_30_out, JAL);
  and and_6 (and_6_out, not_31_out, not_32_out, not_33_out, not_34_out, not_35_out, JALR, not_36_out);
  and and_7 (and_7_out, not_37_out, not_38_out, not_39_out, LUI, not_40_out, not_41_out, not_42_out);
  and and_8 (and_8_out, I, not_43_out, not_44_out, not_45_out, not_46_out, not_47_out, not_48_out);
  and and_9 (and_9_out, not_49_out, not_50_out, not_51_out, not_52_out, not_53_out, not_54_out, JAL);
  and and_10 (and_10_out, not_55_out, not_56_out, not_57_out, not_58_out, not_59_out, JALR, not_60_out);
  and and_11 (and_11_out, not_61_out, not_62_out, not_63_out, not_64_out, LW, not_65_out, not_66_out);
  and and_12 (and_12_out, not_67_out, not_68_out, AUIPC, not_69_out, not_70_out, not_71_out, not_72_out);
  or or_1 (ALU_OP[2], and_1_out, and_2_out, and_3_out, and_4_out);
  or or_2 (ALU_OP[1], and_5_out, and_6_out, and_7_out, and_8_out);
  or or_3 (ALU_OP[0], and_9_out, and_10_out, and_11_out, and_12_out);
endmodule
